# Fritzing sketch breadboard (saved by Fritzing 0.9.4)
breadboards: 1

parts:
  A1 = Waveshare rp2040-zero tht [package=THT]
  Part1 = NRF24L01+ Breakout Board
  WaveShare_1_3inch_OLED_128x1 = WaveShare 1.3inch OLED 128x64
  U1 = mystery part, 3 pins [chip_label=3.3V]

nets:
  N1: A1.Pin_1, U1.pin1
  GND: A1.Pin_2, Part1.GND, WaveShare_1_3inch_OLED_128x1.GND, U1.pin3
  N2: A1.Pin_3, WaveShare_1_3inch_OLED_128x1.VCC
  N3: A1.Pin_4, Part1.CE
  N4: A1.Pin_5, WaveShare_1_3inch_OLED_128x1.RES
  N5: A1.Pin_6, WaveShare_1_3inch_OLED_128x1.D/C
  N6: A1.Pin_12, WaveShare_1_3inch_OLED_128x1.DIN
  N7: A1.Pin_13, WaveShare_1_3inch_OLED_128x1.CLK
  N8: A1.Pin_14, WaveShare_1_3inch_OLED_128x1.CS
  N9: A1.Pin_20, Part1.MOSI
  N10: A1.Pin_21, Part1.SCK
  N11: A1.Pin_22, Part1.CS
  N12: A1.Pin_23, Part1.MISO
  N13: Part1.VCC, U1.pin2

custom parts:
  Waveshare rp2040-zero tht: .RP2040-Zero, A Low-Cost, High-Performance Pico-Like MCU Board Based On Raspberry Pi Microcontroller RP2040. This varant is THT without the extra connections.
  WaveShare 1.3inch OLED 128x64: OLED Original design by Simulz (http://tsblog.simulz.kr) Corrected PCB layout by Andreas Horneffer
