# Fritzing sketch protoboard (saved by Fritzing 0.9.4)
perfboards: 2

parts:
  J19 = female pin header, 9 pins [form="♀ (female)"]
  J20 = female pin header, 9 pins [form="♀ (female)"]
  J22 = female pin header, 3 pins [form="♀ (female)"]
  J23 = female pin header, 4 pins [form="♀ (female)"]
  J24 = female pin header, 3 pins [form="♀ (female)"]
  J21 = female pin header, 7 pins [form="♀ (female)"]
  J31 = female pin header, 9 pins [form="♀ (female)"]  # not connected
  J32 = female pin header, 9 pins [form="♀ (female)"]  # not connected
  J33 = female pin header, 7 pins [form="♀ (female)"]  # not connected
  J34 = female pin header, 3 pins [form="♀ (female)"]  # not connected
  J35 = female pin header, 4 pins [form="♀ (female)"]  # not connected
  J36 = female pin header, 3 pins [form="♀ (female)"]  # not connected

nets:
  N1: J19.pin2, J24.pin2
  N2: J19.pin5, J23.pin4
  N3: J19.pin6, J23.pin2
  N4: J19.pin7, J21.pin1
  N5: J19.pin8, J21.pin2
  N6: J19.pin9, J21.pin3
  N7: J20.pin1, J22.pin3
  N8: J20.pin3, J21.pin7
